# Fritzing sketch arduino connections (saved by Fritzing 0.8.7b)
breadboards: 1

parts:
  Part1 = Arduino Uno (Rev3)
  Part2 = Arduino Uno (Rev3)
  Part3 = Arduino Uno (Rev3)

nets:
  N1: Part1.A4/SDA, Part2.A4/SDA, Part3.A4/SDA
  N2: Part1.A5/SCL, Part2.A5/SCL, Part3.A5/SCL
  5V: Part1.5V, Part2.5V, Part3.5V
  GND: Part1.GND, Part2.GND, Part3.GND

notes:
  Master Arduino
  Slave 1 Arduino
